# Fritzing sketch bluebell_leds_2 (saved by Fritzing 0.8.5b)
circuit board: 5.6cm x 1.8cm
breadboards: 1

parts:
  IC1 = DIP6 [package=DIL]
  IC2 = DIP6 [package=DIL]
  J1 = male pin header, 8 pins [form="♂ (male)"]

nets:
  N1: IC1.1, J1.pin5
  N2: IC1.3, J1.pin4
  N3: IC1.4, J1.pin3
  N4: IC1.6, IC2.6, J1.pin1
  N5: IC2.1, J1.pin8
  N6: IC2.3, J1.pin7
  N7: IC2.4, J1.pin6
