# Fritzing sketch bluebell_main (saved by Fritzing 0.8.5b)
circuit board: 5.6cm x 6.7cm
breadboards: 1

parts:
  9V = male pin header, 1 pin [form="♂ (male)"]
  GND = male pin header, 1 pin [form="♂ (male)"]
  U1 = Voltage Regulator - 5V [package="TO220 [THT]"]
  U2 = MCP1702 Voltage Regulator [package="TO92 [THT]"]
  C1 = Ceramic Capacitor [capacitance=1µF package="100 mil [THT, multilayer]"]
  C2 = Ceramic Capacitor [capacitance=1µF package="100 mil [THT, multilayer]"]
  R1 = Resistor [tolerance=±5% resistance=10k package=THT]
  R2 = Resistor [tolerance=±5% resistance=4.7k package=THT]
  PSWTCH = male pin header, 2 pins [form="♂ (male)"]
  IC1 = ATtiny85 [package=DIL]
  LEDS = female pin header, 8 pins [form="♀ (female)"]
  R3 = Resistor [tolerance=±5% resistance=100 package=THT]
  R4 = Resistor [tolerance=±5% resistance=100 package=THT]
  R5 = Resistor [tolerance=±5% resistance=150 package=THT]
  R6 = Resistor [tolerance=±5% resistance=100 package=THT]
  R7 = Resistor [tolerance=±5% resistance=100 package=THT]
  R8 = Resistor [tolerance=±5% resistance=150 package=THT]
  HC05 = female pin header, 6 pins [form="♀ (female)"]
  Q1 = NPN-Transistor [package="TO92 [THT]"]
  Q2 = NPN-Transistor [package="TO92 [THT]"]
  Q3 = NPN-Transistor [package="TO92 [THT]"]

nets:
  9V_IN: 9V.pin1, PSWTCH.pin1
  GND: GND.pin1, U1.GND, U2.GND, C1.0, C2.0, R2.Pin_1, IC1.GND, HC05.pin1, HC05.pin6, Q1.E, Q2.E, Q3.E
  9V: U1.input_voltage, R1.Pin_0, PSWTCH.pin2
  5V: U1.output_voltage, U2.Vin, C1.1, LEDS.pin1
  3V3: U2.Vout, C2.1, IC1.VCC, HC05.pin2
  M9V: R1.Pin_1, R2.Pin_0, IC1.PB5/RESET
  TX: IC1.PB3, HC05.pin4
  RX: IC1.PB4, HC05.pin5
  BLUE: IC1.PB0/SDA/MOSI, Q1.B
  GREEN: IC1.PB1/MISO, Q2.B
  RED: IC1.PB2/SCL/SCK, Q3.B
  N1: LEDS.pin3, R8.Pin_0
  N2: LEDS.pin4, R7.Pin_0
  N3: LEDS.pin5, R6.Pin_0
  N4: LEDS.pin6, R5.Pin_0
  N5: LEDS.pin7, R4.Pin_0
  N6: LEDS.pin8, R3.Pin_0
  N7: R3.Pin_1, R6.Pin_1, Q1.C
  N8: R4.Pin_1, R7.Pin_1, Q2.C
  N9: R5.Pin_1, R8.Pin_1, Q3.C

custom parts:
  MCP1702 Voltage Regulator: A MCP1702 Low Dropout Fixed Voltage Regulator (available in 1.2V, 1.5V, 1.8V, 2.5V, 2.8V, 3.0V, 3.3V, 4.0V, 5.0V)
